# Fritzing sketch nodemcu-3led (saved by Fritzing 0.9.5d)
breadboards: 2

parts:
  Amica_NodeMCU_DevKit_1_1 = Amica NodeMCU DevKit 1.0
  R1 = Resistor [tolerance=±5% resistance=330 package=THT]
  R2 = Resistor [tolerance=±5% resistance=330 package=THT]
  R3 = Resistor [tolerance=±5% resistance=330 package=THT]
  LED1 = LED - 5mm [color="Red (633nm)" package="5 mm [THT]"]
  LED2 = LED - 5mm [color="Yellow (595nm)" package="5 mm [THT]"]
  LED3 = LED - 5mm [color="Green (565nm)" package="5 mm [THT]"]
  TD-er1 = MH-Z19 CO2 sensor [part_number=MH-Z19]

nets:
  N1: Amica_NodeMCU_DevKit_1_1.pin1, Amica_NodeMCU_DevKit_1_1.pin_10, Amica_NodeMCU_DevKit_1_1.pin_26
  N2: Amica_NodeMCU_DevKit_1_1.pin2, Amica_NodeMCU_DevKit_1_1.pin_9, Amica_NodeMCU_DevKit_1_1.pin_25, Amica_NodeMCU_DevKit_1_1.pin_29, LED1.cathode, LED2.cathode, LED3.cathode, TD-er1.GND
  N3: Amica_NodeMCU_DevKit_1_1.pin6, R3.Pin_1
  N4: Amica_NodeMCU_DevKit_1_1.pin7, R2.Pin_1
  N5: Amica_NodeMCU_DevKit_1_1.pin8, R1.Pin_1
  N6: Amica_NodeMCU_DevKit_1_1.pin_12, TD-er1.RX
  N7: Amica_NodeMCU_DevKit_1_1.pin_13, TD-er1.TX
  N8: Amica_NodeMCU_DevKit_1_1.pin_30, TD-er1.Vin
  N9: R1.Pin_0, LED3.anode
  N10: R2.Pin_0, LED2.anode
  N11: R3.Pin_0, LED1.anode

custom parts:
  Amica NodeMCU DevKit 1.0: Amica NodeMCU DEVKIT 1.0 Development Kit based on ESP8266 ESP-12E, integating GPIO, PWM, IIC, 1-Wire and ADC all in one board.
